# Fritzing sketch 1-MakingAnOscillator (saved by Fritzing 0.9.1b)
breadboards: 1

parts:
  VCC1 = Battery block 9V
  C1 = Ceramic Capacitor [capacitance=100nF package="100 mil [THT, multilayer]"]
  R1 = Resistor [tolerance=±5% resistance=1k package=THT]
  U2 = CD40106 [package=dil14]

nets:
  N1: VCC1.-, C1.0, U2.GND
  N2: VCC1.+, U2.VCC
  N3: C1.1, R1.Pin_0, U2.1A
  N4: R1.Pin_1, U2.1Y
